// Logisim project FelipeRezende.circ as structural Verilog: 6 circuits, main circuit Meio Somador
module Meio_Somador (
  input  A,
  input  B,
  output S,
  output Ts
);

  xor xor_1 (S, A, B);
  and and_1 (Ts, A, B);
endmodule

module Somador_completo (
  input  A,
  input  B,
  input  Te,
  output S,
  output Ts
);

  wire and_1_out, and_2_out, and_3_out, xor_1_out;

  and and_1 (and_1_out, B, Te);
  and and_2 (and_2_out, B, A);
  and and_3 (and_3_out, B, A);
  xor xor_1 (xor_1_out, A, B);
  xor xor_2 (S, xor_1_out, Te);
  or or_1 (Ts, and_1_out, and_2_out, and_3_out);
endmodule

module Somador_4bits (
  input  [3:0] A,
  input  [3:0] B,
  output [3:0] S,
  output C
);

  wire _1_2_ts, Com_2_ts, Com_ts;

  Meio_Somador _1_2 (.A(A[0]), .B(B[0]), .S(S[0]), .Ts(_1_2_ts));
  Somador_completo Com (.A(A[1]), .B(B[1]), .Te(_1_2_ts), .S(S[1]), .Ts(Com_ts));
  Somador_completo Com_2 (.A(A[2]), .B(B[2]), .Te(Com_ts), .S(S[2]), .Ts(Com_2_ts));
  Somador_completo Com_3 (.A(A[3]), .B(B[3]), .Te(Com_2_ts), .S(S[3]), .Ts(C));
endmodule

module Meio_Subtrator (
  input  A,
  input  B,
  output S,
  output Ts
);

  wire not_1_out;

  not not_1 (not_1_out, A);
  xor xor_1 (S, A, B);
  and and_1 (Ts, B, not_1_out);
endmodule

module Subtrator_completo (
  input  A,
  input  B,
  input  Te,
  output S,
  output Ts
);

  wire and_1_out, and_2_out, and_3_out, not_1_out, xor_1_out;

  not not_1 (not_1_out, A);
  and and_1 (and_1_out, B, Te);
  and and_2 (and_2_out, Te, not_1_out);
  and and_3 (and_3_out, B, not_1_out);
  xor xor_1 (xor_1_out, A, B);
  xor xor_2 (S, xor_1_out, Te);
  or or_1 (Ts, and_1_out, and_2_out, and_3_out);
endmodule

module Subtrator_4_bits (
  input  [3:0] A,
  input  [3:0] B,
  output [3:0] S,
  output C
);

  wire _1_2_ts, Com_2_ts, Com_ts;

  Meio_Subtrator _1_2 (.A(A[0]), .B(B[0]), .S(S[0]), .Ts(_1_2_ts));
  Subtrator_completo Com (.A(A[1]), .B(B[1]), .Te(_1_2_ts), .S(S[1]), .Ts(Com_ts));
  Subtrator_completo Com_2 (.A(A[2]), .B(B[2]), .Te(Com_ts), .S(S[2]), .Ts(Com_2_ts));
  Subtrator_completo Com_3 (.A(A[3]), .B(B[3]), .Te(Com_2_ts), .S(S[3]), .Ts(C));
endmodule
